// Digital circuit MUX.dig as structural Verilog
module MUX (
  input  D,
  input  C,
  input  B,
  input  A,
  output Y
);

  wire not_1_out;

  not not_1 (not_1_out, 1'b1);
  Multiplexer #(.Selector_Bits(3)) multiplexer_1 (
    .sel({A, C, D}), .in_0(not_1_out), .in_1(1'b1), .in_2(not_1_out), .in_3(1'b1), .in_4(1'b1),
    .in_5(not_1_out), .in_6(1'b1), .in_7(not_1_out), .out(Y));
  // also tied to GND on the sheet: not_1_out

  // Notes on the sheet:
  //   Use A as the most-significant bit and 
  //   D as the least-significant bit.
  //   Converts between single bits & a 3-bit bus
endmodule

/* Test case:
A B C D Y
0 0 0 0 X
0 0 0 1 1
*/
